# Fritzing sketch 2018-12 Three TRRS Jacks #4 (saved by Fritzing 0.9.3b)
circuit board: 6.90033cm x 1.72155cm
breadboards: 1

parts:
  TRRS1 = Audio Jack (TRRS) 3.5mm [part_number="LUMBERG JEITA RC-5325A" package="RC-5325A [SMD]"]
  J1 = female pin header, 4 pins [form="♀ (female)"]
  J2 = female pin header, 4 pins [form="♀ (female)"]
  TRRS5 = Audio Jack (TRRS) 3.5mm [part_number="LUMBERG JEITA RC-5325A" package="RC-5325A [SMD]"]
  J3 = female pin header, 4 pins [form="♀ (female)"]
  TRRS6 = Audio Jack (TRRS) 3.5mm [part_number="LUMBERG JEITA RC-5325A" package="RC-5325A [SMD]"]
  TRRS4 = Audio Jack (TRRS) 3.5mm [part_number="LUMBERG JEITA RC-5325A" package="RC-5325A [SMD]"]
  TRRS2 = Audio Jack (TRRS) 3.5mm [part_number="LUMBERG JEITA RC-5325A" package="RC-5325A [SMD]"]
  J4 = female pin header, 3 pins [form="♀ (female)"]
  J5 = female pin header, 4 pins [form="♀ (female)"]
  J6 = female pin header, 3 pins [form="♀ (female)"]
  J7 = female pin header, 3 pins [form="♀ (female)"]
  TRRS3 = Audio Jack (TRRS) 3.5mm [part_number=cRC-5325A package="RC-5325A [SMD]"]

nets:
  N1: TRRS1.TIP, J1.pin1, TRRS2.TIP
  N2: TRRS1.SLEEVE, J1.pin4, TRRS2.SLEEVE
  N3: TRRS1.RING1, J1.pin2, TRRS2.RING1
  N4: TRRS1.RING2, J1.pin3, TRRS2.RING2
  N5: J2.pin1, TRRS4.TIP, TRRS3.TIP
  N6: J2.pin2, TRRS4.RING1, TRRS3.RING1
  N7: J2.pin3, TRRS4.RING2, TRRS3.RING2
  N8: J2.pin4, TRRS4.SLEEVE, TRRS3.SLEEVE
  N9: TRRS5.TIP, J3.pin1, TRRS6.TIP, J5.pin1
  N10: TRRS5.SLEEVE, J3.pin4, TRRS6.SLEEVE, J5.pin4
  N11: TRRS5.RING1, J3.pin2, TRRS6.RING1, J5.pin2
  N12: TRRS5.RING2, J3.pin3, TRRS6.RING2, J5.pin3
  N13: J4.pin1, J4.pin2, J4.pin3
  N14: J6.pin1, J6.pin2, J6.pin3
  N15: J7.pin1, J7.pin2, J7.pin3

notes:
  J1
  J2
  J3
  R2
  J5
  J4
  J6
  J7
