# Fritzing sketch Three TRRS Jacks, Prewired (saved by Fritzing 0.9.3b)
circuit board: 4.63683cm x 1.5395cm
breadboards: 1

parts:
  TRRS3 = Audio Jack (TRRS) 3.5mm [part_number="LUMBERG JEITA RC-5325A" package="RC-5325A [SMD]"]
  TRRS2 = Audio Jack (TRRS) 3.5mm [part_number="LUMBERG JEITA RC-5325A" package="RC-5325A [SMD]"]
  J1 = female pin header, 2 pins [form="♀ (female)"]
  J2 = female pin header, 2 pins [form="♀ (female)"]
  TRRS6 = Audio Jack (TRRS) 3.5mm [part_number="LUMBERG JEITA RC-5325A" package="RC-5325A [SMD]"]
  J4 = female pin header, 2 pins [form="♀ (female)"]
  TRRS1 = Audio Jack (TRRS) 3.5mm [part_number="LUMBERG JEITA RC-5325A" package="RC-5325A [SMD]"]
  J3 = female pin header, 2 pins [form="♀ (female)"]
  TRRS4 = Audio Jack (TRRS) 3.5mm [part_number="LUMBERG JEITA RC-5325A" package="RC-5325A [SMD]"]
  TRRS5 = Audio Jack (TRRS) 3.5mm [part_number="LUMBERG JEITA RC-5325A" package="RC-5325A [SMD]"]
  J5 = female pin header, 2 pins [form="♀ (female)"]
  SJ1 = Solder Jumper [package=sj_2s-trace]
  SJ2 = Solder Jumper [package=sj_2s-trace]

nets:
  N1: TRRS3.TIP, TRRS6.TIP, J3.pin1, SJ1.2
  N2: TRRS3.SLEEVE, TRRS2.SLEEVE, TRRS6.SLEEVE, J4.pin2, TRRS5.SLEEVE
  N3: TRRS3.RING1, TRRS2.RING1, TRRS6.RING1, J4.pin1, TRRS5.RING1
  N4: TRRS3.RING2, TRRS6.RING2, J3.pin2, SJ2.2
  N5: TRRS2.TIP, J2.pin1, TRRS5.TIP
  N6: TRRS2.RING2, J2.pin2, TRRS5.RING2
  N7: J1.pin1, TRRS1.TIP, TRRS4.TIP
  N8: J1.pin2, TRRS1.RING2, TRRS4.RING2
  N9: TRRS1.SLEEVE, TRRS4.SLEEVE, J5.pin2, SJ2.1
  N10: TRRS1.RING1, TRRS4.RING1, J5.pin1, SJ1.1

notes:
  Mic Out
  Speaker In
  Earcup-to-Earcup
  Local Mic In
  Local Speaker Out
  +LMic-
  +LSpk-
  Rev1
  Mic
  Spk
  Right Speaker Out
  Right Mic In
  +RMic-
  +RSpk-
  -RSpk+
  -RMic+
